// Logisim project lab11.circ as structural Verilog
module Ex1 (
  input  [7:0] Input,
  output Out1,
  output [7:0] Out2
);

  and and_1 (Out1, Input[0], Input[7]);
  not not_1 (Out2[7], Input[7]);

  assign Out2[6:0] = Input[6:0];
endmodule

module rotr (
  input  [15:0] A,
  input  [3:0] B,
  output [15:0] Output
);

  wire not_1_out, not_2_out, not_3_out, not_4_out;
  wire [15:0] demultiplexer_1_out0, demultiplexer_1_out1, demultiplexer_2_out0, demultiplexer_2_out1,
       demultiplexer_3_out0, demultiplexer_3_out1, demultiplexer_4_out0, demultiplexer_4_out1,
       multiplexer_2_out, multiplexer_3_out, multiplexer_4_out;

  Demultiplexer #(.width(16), .disabled(0), .enable("false")) demultiplexer_1 (
    .out0(demultiplexer_1_out0), .out1(demultiplexer_1_out1), .in(A), .sel(not_1_out));
  not not_1 (not_1_out, B[0]);
  Demultiplexer #(.width(16), .enable("false")) demultiplexer_2 (
    .out0(demultiplexer_2_out0), .out1(demultiplexer_2_out1), .in(multiplexer_3_out), .sel(not_2_out));
  not not_2 (not_2_out, B[3]);
  Demultiplexer #(.width(16), .enable("false")) demultiplexer_3 (
    .out0(demultiplexer_3_out0), .out1(demultiplexer_3_out1), .in(multiplexer_4_out), .sel(not_3_out));
  not not_3 (not_3_out, B[2]);
  Multiplexer #(.width(16), .disabled(0), .enable("false")) multiplexer_1 (
    .in0(demultiplexer_2_out1), .in1({demultiplexer_2_out0[7:0], demultiplexer_2_out0[15:8]}), .out(Output),
    .sel(B[3]));
  Multiplexer #(.width(16), .disabled(0), .enable("false")) multiplexer_2 (
    .in0(demultiplexer_1_out1), .in1({demultiplexer_1_out0[0], demultiplexer_1_out0[15:1]}),
    .out(multiplexer_2_out), .sel(B[0]));
  Multiplexer #(.width(16), .disabled(0), .enable("false")) multiplexer_3 (
    .in0(demultiplexer_3_out1), .in1({demultiplexer_3_out0[3:0], demultiplexer_3_out0[15:4]}),
    .out(multiplexer_3_out), .sel(B[2]));
  Demultiplexer #(.width(16), .disabled(0), .enable("false")) demultiplexer_4 (
    .out0(demultiplexer_4_out0), .out1(demultiplexer_4_out1), .in(multiplexer_2_out), .sel(not_4_out));
  not not_4 (not_4_out, B[1]);
  Multiplexer #(.width(16), .disabled(0), .enable("false")) multiplexer_4 (
    .in0(demultiplexer_4_out1), .in1({demultiplexer_4_out0[1:0], demultiplexer_4_out0[15:2]}),
    .out(multiplexer_4_out), .sel(B[1]));
endmodule

module fib (
  input  [31:0] N,
  output out_2,
  output [31:0] out_3
);

  wire clock_1_out, comparator_1_eq, comparator_1_gt, comparator_1_lt, comparator_2_eq, comparator_2_gt,
       comparator_2_lt;
  wire [31:0] adder_1_out, adder_2_out, bit_extender_1_out, i_q, multiplexer_1_out, x_q, y_q;

  Comparator #(.width(32), .mode("unsigned")) comparator_1 (
    .a(N), .b(i_q), .gt(comparator_1_gt), .eq(comparator_1_eq), .lt(comparator_1_lt));
  Clock clock_1 (.out(clock_1_out));
  or or_1 (out_2, comparator_1_eq, comparator_1_lt);
  Adder #(.width(32)) adder_1 (.a(32'h1), .b(i_q), .out(adder_1_out));  // open: cin, cout
  Register #(.width(32)) x (.D(y_q), .Q(x_q), .clk(clock_1_out));  // open: en, clr
  Register #(.width(32)) i (.D(adder_1_out), .Q(i_q), .clk(clock_1_out));  // open: en, clr
  Comparator #(.width(32), .mode("unsigned")) comparator_2 (
    .a(i_q), .b(32'h1), .gt(comparator_2_gt), .eq(comparator_2_eq), .lt(comparator_2_lt));
  Register #(.width(32)) y (.D(multiplexer_1_out), .Q(y_q), .clk(clock_1_out));  // open: en, clr
  assign bit_extender_1_out = {{31{1'b0}}, comparator_2_lt};  // Bit_Extender bit_extender_1
  Adder #(.width(32)) adder_2 (.a(y_q), .b(out_3), .out(adder_2_out));  // open: cin, cout
  Register #(.width(32)) z (.D(adder_2_out), .Q(out_3), .clk(clock_1_out));  // open: en, clr
  Multiplexer #(.width(32), .disabled(0), .enable("false")) multiplexer_1 (
    .in0(out_3), .in1(bit_extender_1_out), .out(multiplexer_1_out), .sel(comparator_2_lt));
endmodule
